// Logisim project Lab 3 Given.circ as structural Verilog: 6 circuits, main circuit Main
module Main (
);

  wire ALUSrcA, and_1_out, Clock, IorD, IRWrite, MemRead, MemtoReg, MemWrite, PC_Signal, PCWrite,
       PCWriteCond, RegDst, RegWrite, Zero;
  wire [1:0] ALUOp, ALUSrcB, Modified_ALUOp, PCSource;
  wire [3:0] ALUCtl, Current_State, Next_State;
  wire [4:0] Destination_Register, multiplexer_2_out;
  wire [27:0] Stored_PC;
  wire [31:0] A_q, alu_1_aluresult, ALUOut, B, bit_extender_1_out, Data, multiplexer_1_out,
       multiplexer_3_out, multiplexer_4_out, multiplexer_5_out, PC, ram_1_data, register_file_1_rddata1,
       register_file_1_rddata2, shifter_1_out;
  wire [31:2] Extended_Instruction___PC__31_28;
  wire [31:26] Instruction;

  Clock clock_1 (.out(Clock));
  and and_1 (and_1_out, PCWriteCond, Zero);
  or or_1 (PC_Signal, and_1_out, PCWrite);
  Register #(.width(32)) u_PC (
    .D(PC), .en(PC_Signal), .Q({Extended_Instruction___PC__31_28[31:28], Stored_PC}), .clk(Clock));  // open: clr
  // Probe on {Extended_Instruction___PC__31_28[31:28], Stored_PC}
  // Probe on multiplexer_1_out[9:2]
  Multiplexer #(.width(32), .enable("false")) multiplexer_1 (
    .in0({Extended_Instruction___PC__31_28[31:28], Stored_PC}), .in1(ALUOut), .out(multiplexer_1_out),
    .sel(IorD));
  Register #(.width(1)) Next_State_Bit_0 (.D(Next_State[0]), .Q(Current_State[0]), .clk(Clock));  // open: en, clr
  Register #(.width(1)) Next_State_Bit_1 (.D(Next_State[1]), .Q(Current_State[1]), .clk(Clock));  // open: en, clr
  Register #(.width(1)) Next_State_Bit_2 (.D(Next_State[2]), .Q(Current_State[2]), .clk(Clock));  // open: en, clr
  Register #(.width(1)) Next_State_Bit_3 (.D(Next_State[3]), .Q(Current_State[3]), .clk(Clock));  // open: en, clr
  RAM #(.dataWidth(32), .bus("separate")) ram_1 (
    .addr(multiplexer_1_out[9:2]), .din(B), .data(ram_1_data), .str(MemWrite), .clk(Clock), .ld(MemRead));  // open: sel, clr
  // Probe on ram_1_data
  // Probe on ram_1_data
  Register #(.width(32)) IR (
    .D(ram_1_data), .en(IRWrite),
    .Q({Instruction, Extended_Instruction___PC__31_28[27:18], Destination_Register, Extended_Instruction___PC__31_28[12:2]}),
    .clk(Clock));  // open: clr
  Register #(.width(32)) MDR (.D(ram_1_data), .Q(Data), .clk(Clock));  // open: en, clr
  // Probe on Current_State
  // Probe on Data
  // Probe on Extended_Instruction___PC__31_28[7:2]
  // Probe on Extended_Instruction___PC__31_28[12:8]
  // Probe on Destination_Register
  // Probe on Extended_Instruction___PC__31_28[22:18]
  // Probe on Extended_Instruction___PC__31_28[27:23]
  // Probe on Instruction
  // Probe on ALUOut
  // Probe on Data
  // Probe on RegDst
  // Probe on Extended_Instruction___PC__31_28[22:18]
  // Probe on Destination_Register
  // Probe on Extended_Instruction___PC__31_28[27:23]
  // Probe on Extended_Instruction___PC__31_28[22:18]
  Multiplexer #(.width(5), .enable("false")) multiplexer_2 (
    .in0(Extended_Instruction___PC__31_28[22:18]), .in1(Destination_Register), .out(multiplexer_2_out),
    .sel(RegDst));
  // Probe on multiplexer_2_out
  Multiplexer #(.width(32), .enable("false")) multiplexer_3 (
    .in0(ALUOut), .in1(Data), .out(multiplexer_3_out), .sel(MemtoReg));
  Register_File register_file_1 (
    .WrAddr(multiplexer_2_out), .WrData(multiplexer_3_out), .WrReg(RegWrite),
    .RdAddr1(Extended_Instruction___PC__31_28[27:23]), .RdAddr2(Extended_Instruction___PC__31_28[22:18]),
    .RdData1(register_file_1_rddata1), .RdData2(register_file_1_rddata2), .Clock(Clock));
  // Probe on PCSource
  Main_Control main_control_1 (
    .Opcode(Instruction), .Current_State(Current_State), .PC_Source(PCSource), .ALUOp(ALUOp),
    .ALUSrcB(ALUSrcB), .ALUSrcA(ALUSrcA), .RegWrite(RegWrite), .RegDst(RegDst), .MemtoReg(MemtoReg),
    .IRWrite(IRWrite), .MemWrite(MemWrite), .MemRead(MemRead), .IorD(IorD), .PCWrite(PCWrite),
    .PCWriteCond(PCWriteCond), .Next_State(Next_State), .Funct(Extended_Instruction___PC__31_28[7:2]));
  // Probe on RegWrite
  // Probe on MemtoReg
  // Probe on IRWrite
  // Probe on MemWrite
  // Probe on MemRead
  // Probe on IorD
  // Probe on PCWrite
  // Probe on PCWriteCond
  // Probe on Next_State
  // Probe on ALUOp
  // Probe on ALUSrcB
  // Probe on ALUSrcA
  // Probe on RegDst
  // Probe on register_file_1_rddata1
  // Probe on register_file_1_rddata2
  // Probe on bit_extender_1_out
  // Probe on {Destination_Register, Extended_Instruction___PC__31_28[12:2]}
  Register #(.width(32)) A (.D(register_file_1_rddata1), .Q(A_q), .clk(Clock));  // open: en, clr
  Register #(.width(32)) u_B (.D(register_file_1_rddata2), .Q(B), .clk(Clock));  // open: en, clr
  assign bit_extender_1_out = {{16{1'b0}}, {Destination_Register, Extended_Instruction___PC__31_28[12:2]}};  // Bit_Extender bit_extender_1
  // Probe on bit_extender_1_out
  // Probe on {Extended_Instruction___PC__31_28[27:18], Destination_Register, Extended_Instruction___PC__31_28[12:2]}
  Shifter #(.width(32)) shifter_1 (.in(bit_extender_1_out), .\dist (5'b00010), .out(shifter_1_out));
  // Probe on Modified_ALUOp
  // Probe on Extended_Instruction___PC__31_28[7:2]
  Multiplexer #(.width(32), .enable("false")) multiplexer_4 (
    .in0({Extended_Instruction___PC__31_28[31:28], Stored_PC}), .in1(A_q), .out(multiplexer_4_out),
    .sel(ALUSrcA));
  Multiplexer #(.select(2), .width(32), .enable("false")) multiplexer_5 (
    .in0(B), .in1(32'h4), .in2(bit_extender_1_out), .in3(shifter_1_out), .out(multiplexer_5_out),
    .sel(ALUSrcB));
  // Probe on shifter_1_out
  // Probe on {Extended_Instruction___PC__31_28[27:18], Destination_Register, Extended_Instruction___PC__31_28[12:2], 2'b00}
  // Probe on multiplexer_4_out
  Multiplexer #(.select(5), .width(2), .enable("false")) multiplexer_6 (
    .in0(ALUOp), .in1(ALUOp), .in2(ALUOp), .in3(ALUOp), .in4(ALUOp), .in5(ALUOp), .in6(ALUOp), .in7(ALUOp),
    .in8(2'b00), .in9(ALUOp), .in10(2'b11), .in11(ALUOp), .in12(2'b01), .in13(2'b10), .in14(ALUOp),
    .in15(ALUOp), .in16(ALUOp), .in17(ALUOp), .in18(ALUOp), .in19(ALUOp), .in20(ALUOp), .in21(ALUOp),
    .in22(ALUOp), .in23(ALUOp), .in24(ALUOp), .in25(ALUOp), .in26(ALUOp), .in27(ALUOp), .in28(ALUOp),
    .in29(ALUOp), .in30(ALUOp), .in31(ALUOp), .out(Modified_ALUOp), .sel(Instruction[30:26]));
  // Probe on ALUCtl
  ALU alu_1 (
    .ALUCtl(ALUCtl), .A(multiplexer_4_out), .B(multiplexer_5_out), .ALUResult(alu_1_aluresult), .Zero(Zero),
    .Shamt({5{1'b0}}));  // open: Overflow
  // Probe on multiplexer_5_out
  // Probe on {Extended_Instruction___PC__31_28[31:18], Destination_Register, Extended_Instruction___PC__31_28[12:2], 2'b00}
  ALU_Control alu_control_1 (.ALUOp(Modified_ALUOp), .Funct(Extended_Instruction___PC__31_28[7:2]), .ALUCtl(ALUCtl));
  // Probe on ALUCtl
  // Probe on alu_1_aluresult
  // Probe on alu_1_aluresult
  Register #(.width(32)) u_ALUOut (.D(alu_1_aluresult), .Q(ALUOut), .clk(Clock));  // open: en, clr
  // Probe on {Extended_Instruction___PC__31_28[31:18], Destination_Register, Extended_Instruction___PC__31_28[12:2], 2'b00}
  // Probe on ALUOut
  Multiplexer #(.select(2), .width(32), .enable("false")) multiplexer_7 (
    .in0(alu_1_aluresult), .in1(ALUOut),
    .in2({Extended_Instruction___PC__31_28[31:18], Destination_Register, Extended_Instruction___PC__31_28[12:2], 2'b00}),
    .out(PC), .sel(PCSource));  // open: in3
  // Probe on nothing
  // Probe on nothing
  // Probe on nothing
  // Probe on nothing
  // Probe on nothing
  // Probe on nothing
  // Probe on nothing
  // Probe on nothing
  // Probe on nothing
  // Probe on nothing

  // Other names for the same wires on the sheet: Current_State_0 = Current_State[0];
  //   Current_State_1 = Current_State[1]; Current_State_2 = Current_State[2]; Current_State_3 = Current_State[3];
  //   Funct[5:0] = Extended_Instruction___PC__31_28[7:2];
  //   Instruction[25:0] = {Extended_Instruction___PC__31_28[27:18], Destination_Register, Extended_Instruction___PC__31_28[12:2]};
  //   Instruction__15_0[15:0] = {Destination_Register, Extended_Instruction___PC__31_28[12:2]};
  //   Instruction__25_0[25:0] = {Extended_Instruction___PC__31_28[27:18], Destination_Register, Extended_Instruction___PC__31_28[12:2]};
  //   Shmt[4:0] = Extended_Instruction___PC__31_28[12:8];
  //   Extended_Instruction___PC__31_28[17:13] = Destination_Register;
  //   Target_Register[4:0] = Extended_Instruction___PC__31_28[22:18];
  //   Source_Register[4:0] = Extended_Instruction___PC__31_28[27:23];
  //   PC__31_28[3:0] = Extended_Instruction___PC__31_28[31:28];
  //   Stored_PC[31:28] = Extended_Instruction___PC__31_28[31:28]; Opcode[5:0] = Instruction;
  //   Next_State_0 = Next_State[0]; Next_State_1 = Next_State[1]; Next_State_2 = Next_State[2];
  //   Next_State_3 = Next_State[3]
endmodule

module ALU (
  input  [3:0] ALUCtl,
  input  [31:0] A,
  input  [31:0] B,
  input  [4:0] Shamt,
  output [31:0] ALUResult,
  output Zero,
  output Overflow
);

  wire comparator_1_lt, comparator_2_lt, comparator_3_eq, comparator_4_eq, or_2_out;
  wire [31:0] ADD, AND, NOR, OR, SLL, SLT, SLTU, SRL, SUB, XOR;

  // Probe on ALUCtl
  assign NOR = ~(A | B);  // NOR_Gate nor_1, 32 bits wide
  Adder #(.width(32)) adder_1 (.a(A), .b(B), .out(ADD));  // open: cin, cout
  Subtractor #(.width(32)) subtractor_1 (.a(A), .b(B), .out(SUB));  // open: bin, bout
  assign AND = A & B;  // AND_Gate and_1, 32 bits wide
  assign OR = A | B;  // OR_Gate or_1, 32 bits wide
  assign XOR = A ^ B;  // XOR_Gate xor_1, 32 bits wide
  Comparator #(.width(32)) comparator_1 (.a(A), .b(B), .lt(comparator_1_lt));  // open: gt, eq
  assign SLT = {{31{1'b0}}, comparator_1_lt};  // Bit_Extender bit_extender_1
  Shifter #(.width(32)) shifter_1 (.in(B), .\dist (Shamt), .out(SLL));
  Shifter #(.width(32), .shift("lr")) shifter_2 (.in(B), .\dist (Shamt), .out(SRL));
  Comparator #(.width(32), .mode("unsigned")) comparator_2 (.a(A), .b(B), .lt(comparator_2_lt));  // open: gt, eq
  assign SLTU = {{31{1'b0}}, comparator_2_lt};  // Bit_Extender bit_extender_2
  Multiplexer #(.select(4), .width(32), .enable("false")) multiplexer_1 (
    .in0(XOR), .in1(SLTU), .in2(SLT), .in3(AND), .in4(NOR), .in5(SUB), .in6(OR), .in7(ADD), .in8(SRL),
    .in9(SLL), .out(ALUResult), .sel(ALUCtl));  // open: in10, in11, in12, in13, in14, in15
  Comparator #(.width(4)) comparator_3 (.a(4'b0111), .b(ALUCtl), .eq(comparator_3_eq));  // open: gt, lt
  Comparator #(.width(4)) comparator_4 (.a(ALUCtl), .b(4'b0101), .eq(comparator_4_eq));  // open: gt, lt
  Overflow_Unit overflow_unit_1 (
    .Add(comparator_3_eq), .Sub(comparator_4_eq), .ASign(A[31]), .BSign(B[31]), .ResultSign(ALUResult[31]),
    .Overflow(Overflow));
  or or_2 (or_2_out, ALUResult[0], ALUResult[1], ALUResult[2], ALUResult[3], ALUResult[4], ALUResult[5], ALUResult[6], ALUResult[7], ALUResult[8], ALUResult[9], ALUResult[10], ALUResult[11], ALUResult[12], ALUResult[13], ALUResult[14], ALUResult[15], ALUResult[16], ALUResult[17], ALUResult[18], ALUResult[19], ALUResult[20], ALUResult[21], ALUResult[22], ALUResult[23], ALUResult[24], ALUResult[25], ALUResult[26], ALUResult[27], ALUResult[28], ALUResult[29], ALUResult[30], ALUResult[31]);
  not not_1 (Zero, or_2_out);

  // Other names for the same wires on the sheet: ASign = A[31]; ResultSign = ALUResult[31]; BSign = B[31]

  // Notes on the sheet:
  //   ALUCtl for ADD for top port
  //   ALUCtl for SUB for second port
endmodule

module Register_File (
  input  [4:0] WrAddr,
  input  [31:0] WrData,
  input  WrReg,
  input  [4:0] RdAddr1,
  input  [4:0] RdAddr2,
  input  Clock,
  output [31:0] RdData1,
  output [31:0] RdData2
);

  wire WrReg0, WrReg1, WrReg2, WrReg3, WrReg4, WrReg5, WrReg6, WrReg7, WrReg8, WrReg9, WrReg10, WrReg11,
       WrReg12, WrReg13, WrReg14, WrReg15, WrReg16, WrReg17, WrReg18, WrReg19, WrReg20, WrReg21, WrReg22,
       WrReg23, WrReg24, WrReg25, WrReg26, WrReg27, WrReg28, WrReg29, WrReg30, WrReg31;
  wire [31:0] RegData1, RegData2, RegData3, RegData4, RegData5, RegData6, RegData7, RegData8, RegData9,
       RegData10, RegData11, RegData12, RegData13, RegData14, RegData15, RegData16, RegData17, RegData18,
       RegData19, RegData20, RegData21, RegData22, RegData23, RegData24, RegData25, RegData26, RegData27,
       RegData28, RegData29, RegData30, RegData31;

  Demultiplexer #(.select(5), .enable("false")) demultiplexer_1 (
    .out0(WrReg0), .out1(WrReg1), .out2(WrReg2), .out3(WrReg3), .out4(WrReg4), .out5(WrReg5), .out6(WrReg6),
    .out7(WrReg7), .out8(WrReg8), .out9(WrReg9), .out10(WrReg10), .out11(WrReg11), .out12(WrReg12),
    .out13(WrReg13), .out14(WrReg14), .out15(WrReg15), .out16(WrReg16), .out17(WrReg17), .out18(WrReg18),
    .out19(WrReg19), .out20(WrReg20), .out21(WrReg21), .out22(WrReg22), .out23(WrReg23), .out24(WrReg24),
    .out25(WrReg25), .out26(WrReg26), .out27(WrReg27), .out28(WrReg28), .out29(WrReg29), .out30(WrReg30),
    .out31(WrReg31), .in(WrReg), .sel(WrAddr));
  // Probe on RegData4
  Register #(.width(32)) Reg4 (.D(WrData), .en(WrReg4), .Q(RegData4), .clk(Clock));  // open: clr
  // Probe on RegData8
  Register #(.width(32)) Reg8 (.D(WrData), .en(WrReg8), .Q(RegData8), .clk(Clock));  // open: clr
  // Probe on RegData12
  Register #(.width(32)) Reg12 (.D(WrData), .en(WrReg12), .Q(RegData12), .clk(Clock));  // open: clr
  // Probe on RegData16
  Register #(.width(32)) Reg16 (.D(WrData), .en(WrReg16), .Q(RegData16), .clk(Clock));  // open: clr
  // Probe on RegData20
  Register #(.width(32)) Reg20 (.D(WrData), .en(WrReg20), .Q(RegData20), .clk(Clock));  // open: clr
  // Probe on RegData24
  Register #(.width(32)) Reg24 (.D(WrData), .en(WrReg24), .Q(RegData24), .clk(Clock));  // open: clr
  // Probe on RegData28
  Register #(.width(32)) Reg28 (.D(WrData), .en(WrReg28), .Q(RegData28), .clk(Clock));  // open: clr
  Register #(.width(32)) Reg1 (.D(WrData), .en(WrReg1), .Q(RegData1), .clk(Clock));  // open: clr
  Register #(.width(32)) Reg5 (.D(WrData), .en(WrReg5), .Q(RegData5), .clk(Clock));  // open: clr
  Register #(.width(32)) Reg9 (.D(WrData), .en(WrReg9), .Q(RegData9), .clk(Clock));  // open: clr
  Register #(.width(32)) Reg13 (.D(WrData), .en(WrReg13), .Q(RegData13), .clk(Clock));  // open: clr
  Register #(.width(32)) Reg17 (.D(WrData), .en(WrReg17), .Q(RegData17), .clk(Clock));  // open: clr
  Register #(.width(32)) Reg21 (.D(WrData), .en(WrReg21), .Q(RegData21), .clk(Clock));  // open: clr
  Register #(.width(32)) Reg25 (.D(WrData), .en(WrReg25), .Q(RegData25), .clk(Clock));  // open: clr
  Register #(.width(32)) Reg29 (.D(WrData), .en(WrReg29), .Q(RegData29), .clk(Clock));  // open: clr
  // Probe on RegData1
  // Probe on RegData5
  // Probe on RegData9
  // Probe on RegData13
  // Probe on RegData17
  // Probe on RegData21
  // Probe on RegData25
  // Probe on RegData29
  // Probe on RegData2
  Register #(.width(32)) Reg2 (.D(WrData), .en(WrReg2), .Q(RegData2), .clk(Clock));  // open: clr
  // Probe on RegData6
  Register #(.width(32)) Reg6 (.D(WrData), .en(WrReg6), .Q(RegData6), .clk(Clock));  // open: clr
  // Probe on RegData10
  Register #(.width(32)) Reg10 (.D(WrData), .en(WrReg10), .Q(RegData10), .clk(Clock));  // open: clr
  // Probe on RegData14
  Register #(.width(32)) Reg14 (.D(WrData), .en(WrReg14), .Q(RegData14), .clk(Clock));  // open: clr
  // Probe on RegData18
  Register #(.width(32)) Reg18 (.D(WrData), .en(WrReg18), .Q(RegData18), .clk(Clock));  // open: clr
  // Probe on RegData22
  Register #(.width(32)) Reg22 (.D(WrData), .en(WrReg22), .Q(RegData22), .clk(Clock));  // open: clr
  // Probe on RegData26
  Register #(.width(32)) Reg26 (.D(WrData), .en(WrReg26), .Q(RegData26), .clk(Clock));  // open: clr
  // Probe on RegData30
  Register #(.width(32)) Reg30 (.D(WrData), .en(WrReg30), .Q(RegData30), .clk(Clock));  // open: clr
  // Probe on RegData3
  Register #(.width(32)) Reg3 (.D(WrData), .en(WrReg3), .Q(RegData3), .clk(Clock));  // open: clr
  // Probe on RegData7
  Register #(.width(32)) Reg7 (.D(WrData), .en(WrReg7), .Q(RegData7), .clk(Clock));  // open: clr
  // Probe on RegData11
  Register #(.width(32)) Reg11 (.D(WrData), .en(WrReg11), .Q(RegData11), .clk(Clock));  // open: clr
  // Probe on RegData15
  Register #(.width(32)) Reg15 (.D(WrData), .en(WrReg15), .Q(RegData15), .clk(Clock));  // open: clr
  // Probe on RegData19
  Register #(.width(32)) Reg19 (.D(WrData), .en(WrReg19), .Q(RegData19), .clk(Clock));  // open: clr
  // Probe on RegData23
  Register #(.width(32)) Reg23 (.D(WrData), .en(WrReg23), .Q(RegData23), .clk(Clock));  // open: clr
  // Probe on RegData27
  Register #(.width(32)) Reg27 (.D(WrData), .en(WrReg27), .Q(RegData27), .clk(Clock));  // open: clr
  // Probe on RegData31
  Register #(.width(32)) Reg31 (.D(WrData), .en(WrReg31), .Q(RegData31), .clk(Clock));  // open: clr
  Multiplexer #(.select(5), .width(32), .enable("false")) multiplexer_1 (
    .in0({32{1'b0}}), .in1(RegData1), .in2(RegData2), .in3(RegData3), .in4(RegData4), .in5(RegData5),
    .in6(RegData6), .in7(RegData7), .in8(RegData8), .in9(RegData9), .in10(RegData10), .in11(RegData11),
    .in12(RegData12), .in13(RegData13), .in14(RegData14), .in15(RegData15), .in16(RegData16),
    .in17(RegData17), .in18(RegData18), .in19(RegData19), .in20(RegData20), .in21(RegData21),
    .in22(RegData22), .in23(RegData23), .in24(RegData24), .in25(RegData25), .in26(RegData26),
    .in27(RegData27), .in28(RegData28), .in29(RegData29), .in30(RegData30), .in31(RegData31), .out(RdData1),
    .sel(RdAddr1));
  Multiplexer #(.select(5), .width(32), .enable("false")) multiplexer_2 (
    .in0({32{1'b0}}), .in1(RegData1), .in2(RegData2), .in3(RegData3), .in4(RegData4), .in5(RegData5),
    .in6(RegData6), .in7(RegData7), .in8(RegData8), .in9(RegData9), .in10(RegData10), .in11(RegData11),
    .in12(RegData12), .in13(RegData13), .in14(RegData14), .in15(RegData15), .in16(RegData16),
    .in17(RegData17), .in18(RegData18), .in19(RegData19), .in20(RegData20), .in21(RegData21),
    .in22(RegData22), .in23(RegData23), .in24(RegData24), .in25(RegData25), .in26(RegData26),
    .in27(RegData27), .in28(RegData28), .in29(RegData29), .in30(RegData30), .in31(RegData31), .out(RdData2),
    .sel(RdAddr2));
endmodule

module Overflow_Unit (
  input  Add,
  input  Sub,
  input  ASign,
  input  BSign,
  input  ResultSign,
  output Overflow
);

  wire and_1_out, and_2_out, or_1_out, xnor_1_out, xor_1_out, xor_2_out;

  xnor xnor_1 (xnor_1_out, ASign, BSign);
  xor xor_1 (xor_1_out, ASign, BSign);
  and and_1 (and_1_out, xnor_1_out, Add);
  and and_2 (and_2_out, xor_1_out, Sub);
  or or_1 (or_1_out, and_1_out, and_2_out);
  xor xor_2 (xor_2_out, ResultSign, ASign);
  and and_3 (Overflow, or_1_out, xor_2_out);

  // Notes on the sheet:
  //   Overflow occurs when doing addition and sign(A) == sign(B) && sign(result) != sign(A)
  //   Or
  //   Overflow occurs when doing subtraction and sign(A) != sign(B) && sign(result) != sign(A)
endmodule

module ALU_Control (
  input  [1:0] ALUOp,
  input  [5:0] Funct,
  output [3:0] ALUCtl
);

  wire and_2_out, and_3_out, and_4_out, and_5_out, and_6_out, and_7_out, and_8_out, and_9_out, and_10_out,
       and_11_out, and_12_out, and_13_out, and_14_out, and_15_out, and_16_out, and_17_out, and_18_out,
       and_19_out, and_20_out, not_1_out, not_2_out, not_3_out, not_4_out, not_5_out, not_6_out, not_7_out,
       not_8_out, not_9_out, not_10_out, not_11_out, not_12_out, not_13_out, not_14_out, not_15_out,
       not_16_out, not_17_out, not_18_out, not_19_out, not_20_out, not_21_out, not_22_out, not_23_out,
       not_24_out, not_25_out, not_26_out, not_27_out, not_28_out, not_29_out, not_30_out, not_31_out,
       not_32_out, not_33_out, not_34_out, not_35_out, not_36_out, not_37_out, not_38_out, not_39_out,
       not_40_out, not_41_out, not_42_out, not_43_out, not_44_out, not_45_out, not_46_out;

  not not_1 (not_1_out, Funct[5]);
  not not_2 (not_2_out, Funct[4]);
  not not_3 (not_3_out, Funct[3]);
  not not_4 (not_4_out, Funct[2]);
  not not_5 (not_5_out, Funct[0]);
  not not_6 (not_6_out, ALUOp[1]);
  not not_7 (not_7_out, ALUOp[0]);
  not not_8 (not_8_out, ALUOp[0]);
  not not_9 (not_9_out, Funct[3]);
  not not_10 (not_10_out, ALUOp[0]);
  not not_11 (not_11_out, Funct[5]);
  not not_12 (not_12_out, ALUOp[0]);
  not not_13 (not_13_out, Funct[5]);
  not not_14 (not_14_out, ALUOp[0]);
  not not_15 (not_15_out, Funct[1]);
  not not_16 (not_16_out, ALUOp[0]);
  not not_17 (not_17_out, ALUOp[0]);
  not not_18 (not_18_out, Funct[4]);
  not not_19 (not_19_out, Funct[3]);
  not not_20 (not_20_out, Funct[2]);
  not not_21 (not_21_out, Funct[0]);
  not not_22 (not_22_out, Funct[4]);
  not not_23 (not_23_out, Funct[3]);
  not not_24 (not_24_out, Funct[3]);
  not not_25 (not_25_out, Funct[2]);
  not not_26 (not_26_out, Funct[5]);
  not not_27 (not_27_out, Funct[5]);
  not not_28 (not_28_out, Funct[0]);
  not not_29 (not_29_out, Funct[1]);
  not not_30 (not_30_out, Funct[4]);
  not not_31 (not_31_out, Funct[3]);
  not not_32 (not_32_out, Funct[2]);
  not not_33 (not_33_out, Funct[1]);
  not not_34 (not_34_out, Funct[0]);
  not not_35 (not_35_out, Funct[4]);
  not not_36 (not_36_out, Funct[3]);
  not not_37 (not_37_out, Funct[2]);
  not not_38 (not_38_out, Funct[0]);
  not not_39 (not_39_out, Funct[4]);
  not not_40 (not_40_out, Funct[3]);
  not not_41 (not_41_out, Funct[1]);
  not not_42 (not_42_out, Funct[0]);
  not not_43 (not_43_out, Funct[4]);
  not not_44 (not_44_out, Funct[2]);
  and and_1 (ALUCtl[3], ALUOp[1], not_1_out, not_2_out, not_3_out, not_4_out, not_5_out);
  and and_2 (and_2_out, not_6_out, not_7_out);
  and and_3 (and_3_out, not_8_out, not_9_out, Funct[0]);
  and and_4 (and_4_out, not_10_out, not_11_out, Funct[2]);
  and and_5 (and_5_out, not_12_out, not_13_out, Funct[3]);
  and and_6 (and_6_out, not_14_out, Funct[3], not_15_out);
  and and_7 (and_7_out, not_16_out, Funct[3], Funct[2]);
  and and_8 (and_8_out, not_17_out, Funct[4]);
  and and_9 (and_9_out, ALUOp[1], Funct[5], not_18_out, not_19_out, not_20_out, not_21_out);
  and and_10 (and_10_out, ALUOp[1], Funct[5], not_22_out, not_23_out, Funct[2], Funct[0]);
  not not_45 (not_45_out, ALUOp[1]);
  and and_11 (and_11_out, not_24_out, not_25_out, Funct[0]);
  and and_12 (and_12_out, not_26_out, Funct[2]);
  and and_13 (and_13_out, not_27_out, Funct[3]);
  and and_14 (and_14_out, Funct[3], not_28_out);
  and and_15 (and_15_out, Funct[3], Funct[2]);
  and and_16 (and_16_out, Funct[5], not_29_out);
  not not_46 (not_46_out, ALUOp[1]);
  and and_17 (and_17_out, not_30_out, not_31_out, not_32_out, not_33_out, not_34_out);
  and and_18 (and_18_out, Funct[5], not_35_out, not_36_out, not_37_out, not_38_out);
  and and_19 (and_19_out, Funct[5], not_39_out, not_40_out, not_41_out, not_42_out);
  and and_20 (and_20_out, Funct[5], not_43_out, Funct[3], not_44_out, Funct[1], Funct[0]);
  or or_1 (ALUCtl[2], and_2_out, and_3_out, and_4_out, and_5_out, and_6_out, and_7_out, and_8_out, and_9_out, and_10_out);
  or or_2 (ALUCtl[1], not_45_out, and_11_out, and_12_out, and_13_out, and_14_out, and_15_out, Funct[4], and_16_out);
  or or_3 (ALUCtl[0], not_46_out, and_17_out, and_18_out, and_19_out, and_20_out);

  // Other names for the same wires on the sheet: F0 = Funct[0]; F1 = Funct[1]; F2 = Funct[2]; F3 = Funct[3];
  //   F4 = Funct[4]; F5 = Funct[5]
endmodule

module Main_Control (
  input  [5:0] Opcode,
  input  [3:0] Current_State,
  input  [5:0] Funct,
  output [1:0] PC_Source,
  output [1:0] ALUOp,
  output [1:0] ALUSrcB,
  output ALUSrcA,
  output RegWrite,
  output RegDst,
  output MemtoReg,
  output IRWrite,
  output MemWrite,
  output MemRead,
  output IorD,
  output PCWrite,
  output PCWriteCond,
  output [3:0] Next_State
);

  ROM #(.addrWidth(16), .dataWidth(20)) rom_1 (
    .addr({Current_State, Opcode, Funct}),
    .data({Next_State, PC_Source, ALUOp, ALUSrcB, ALUSrcA, MemRead, RegWrite, RegDst, MemtoReg, IRWrite, MemWrite, IorD, PCWrite, PCWriteCond}));  // open: sel

  // Other names for the same wires on the sheet: Address_Bit_Width[15:0] = {Current_State, Opcode, Funct};
  //   ALUOp_0 = ALUOp[0]; ALUOp_1 = ALUOp[1]; ALUSrcB_0 = ALUSrcB[0]; ALUSrcB_1 = ALUSrcB[1];
  //   Next_State_0 = Next_State[0]; Next_State_1 = Next_State[1]; Next_State_2 = Next_State[2];
  //   Next_State_3 = Next_State[3]; PC_Source_0 = PC_Source[0]; PC_Source_1 = PC_Source[1]

  // Notes on the sheet:
  //   contents of rom_1 (hex, n*v repeats v):
  //   48*10512 464*10502 64*10512 64*10502 64*10512 64*10502 128*10512 2752*10502 10501 270*10502 0
  //   176*10502 32*0 60c00 0 60c00 0 4*60c00 0 0 60c00 60c00 84*0 64*90c00 64*0 64*80c00 192*0 64*a0c00
  //   64*0 64*a0c00 64*0 128*a0c00 1344*0 64*20c00 448*0 64*20c00 3520*0 64*30a00 448*0 64*50a00 3520*0
  //   64*40104 4032*0 64*c0 4544*0 64*c 1280*0 72200 0 72200 29*0 72200 0 72200 0 4*72200 0 0 72200 72200
  //   4052*0 c0 0 c0 29*0 c0 0 c0 0 4*c0 0 0 c0 c0 468*0 64*c0 64*0 64*c0 64*0 128*c0 3456*0 64*5201
  //   3904*0 64*8002 4416*0 64*b2a00 64*0 64*b2a00 64*0 128*b2a00 3712*0 64*80 64*0 64*80 64*0 128*80
endmodule
